# Fritzing sketch Robi (saved by Fritzing 0.9.5d)

parts:
  Mod1 = Raspberry Pi Pico
  L298N1 = L298N DC motor driver
  D1 = Rectifier Diode [part_number=1N4001 package="Melf DO-213 AB [SMD]"]
  VCC1 = Battery
  M2 = DC Motor
  M1 = DC Motor
  S1 = Pushbutton [package="[THT]"]

nets:
  N1: Mod1.pin_1, S1.Pin_2
  N2: Mod1.pin_3, Mod1.pin_38, Mod1.pin_42, L298N1.GND, VCC1.-, S1.Pin_4
  N3: Mod1.pin_24, L298N1.IN4
  N4: Mod1.pin_25, L298N1.IN3
  N5: Mod1.pin_26, L298N1.IN2
  N6: Mod1.pin_27, L298N1.IN1
  N7: Mod1.pin_39, D1.cathode
  N8: L298N1.OUT1, M2.pin_2
  N9: L298N1.OUT2, M2.pin_1
  N10: L298N1.OUT3, M1.pin_2
  N11: L298N1.OUT4, M1.pin_1
  N12: L298N1.5V, D1.anode, VCC1.+

custom parts:
  Raspberry Pi Pico: Raspberry Pi Pico. Based around the RP2040 microcontroller the Pico is a low cost microcontroller device bringing Raspberry Pi quality, cost, and easy of use to the microcontroller space. Jan 2021, Split part in to two versions: tht (this one) and SMD. This one will drill holes for a .1 in header in pcb to allow plugging in the module as well as providing pads to solder the module to the top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
  L298N DC motor driver: 2x DC motor driver with 78M05 positive voltage regulator (7..35 V) L298N: max 46 V, 2 A Set 5 V Enable jumper to enable 5 V regultor (needed for the L298N) and +5 V output at screw terminal or supply external +5 V at screw terminal Set ENA and/or ENB to +5 V to enable motor permanently or supply ENA and/or ENB with PWM signal IN1 and IN2 set rotation directory for motor A (OUT1/OUT2) IN2 and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
